# Fritzing sketch phoneCodeOscillatorTrinketPro (saved by Fritzing 0.9.2b)
circuit board: 4.83496cm x 4.20035cm
breadboards: 1

parts:
  C1 = Ceramic Capacitor [capacitance=10µF package="100 mil [THT, multilayer]"]
  Volume = Trimmer Potentiometer [maximum_resistance=10kΩ package=THT]
  C2 = Ceramic Capacitor [capacitance=0.1µF package="100 mil [THT, multilayer]"]
  R2 = Resistor [tolerance=±5% resistance=68 package=THT]
  KeyInputJack = Audio Jack (TRS) 3.5mm [package="4Ucon 08780 [THT]"]
  SignalOut = TRRS 3.5mm Jack Breakout
  Part3 = Pro Trinket 3.3V
  Piezo = Piezo Speaker
  Sidetone_Mon = Audio Jack (TRS) 3.5mm [package="4Ucon 08780 [THT]"]
  Mute = Toggle Switch [package=THT]
  U2 = POT [package=alps_pot]  # not connected
  R4 = Rotary Potentiometer (Small) [maximum_resistance=100kΩ package=THT]  # not connected
  U3 = POT [package=pot_alpha_rv16af-20]  # not connected

nets:
  N1: C1.0, Volume.wiper
  N2: C1.1, SignalOut.SLEEVE, Mute.COM
  N3: Volume.leg1, C2.0, R2.Pin_1
  N4: Volume.leg2, C2.1, KeyInputJack.Sleeve, SignalOut.RING2, Part3.RESET, Piezo.pin1, Sidetone_Mon.Sleeve
  N5: R2.Pin_0, Part3.D9
  N6: KeyInputJack.Ring, Part3.D11
  N7: KeyInputJack.Tip, Part3.D10
  N8: Piezo.pin2, Mute.L2
  N9: Sidetone_Mon.Ring, Sidetone_Mon.Tip, Mute.L1

custom parts:
  Pro Trinket 3.3V: The Pro Trinket 3.3V is like an Arduino Pro Mini with more pins and USB included. However, it uses 3V logic and 12MHz clock which means it's good when you want a lower-power and lower-voltage setup. Built with the common core Arduino chip, the ATmega328p, it has 18 GPIO, 2 extra analog inputs, 28K of flash, and 2K of RAM. It has onboard USB bootloading support with Optiboot support, so you can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
