# Fritzing sketch phoneCodeOscillatorTrinketProSMD (saved by Fritzing 0.9.2b)
circuit board: 4.49114cm x 4.09616cm
breadboards: 1

parts:
  Part3 = Pro Trinket 3.3V
  Piezo = Piezo Speaker
  Mute = Toggle Switch [package=THT]
  R2 = Resistor [tolerance=±10% resistance=68 package="0603 [SMD]"]
  C2 = Ceramic Capacitor [capacitance=0.1µF package="0603 [SMD, multilayer]"]
  C1 = Ceramic Capacitor [capacitance=10µF package="0603 [SMD, multilayer]"]
  Volume = Trimmer Potentiometer [maximum_resistance=10kΩ package=THT]
  KeyInputJack = Audio Jack (TRRS) 3.5mm [part_number="LUMBERG JEITA RC-5325A" package="RC-5325A [SMD]"]  # not connected
  Sidetone_Mon = Audio Jack (TRRS) 3.5mm [part_number="LUMBERG JEITA RC-5325A" package="RC-5325A [SMD]"]
  Sidetone_Mon1 = Audio Jack (TRRS) 3.5mm [part_number="LUMBERG JEITA RC-5325A" package="RC-5325A [SMD]"]  # not connected

nets:
  N1: Part3.RESET, Piezo.pin1, C2.1, Volume.leg2
  N2: Part3.D9, R2.Pin_0
  N3: Piezo.pin2, Mute.L2
  N4: Mute.L1, Sidetone_Mon.TIP
  N5: Mute.COM, C1.1
  N6: R2.Pin_1, C2.0, Volume.leg1
  N7: C1.0, Volume.wiper

custom parts:
  Pro Trinket 3.3V: The Pro Trinket 3.3V is like an Arduino Pro Mini with more pins and USB included. However, it uses 3V logic and 12MHz clock which means it's good when you want a lower-power and lower-voltage setup. Built with the common core Arduino chip, the ATmega328p, it has 18 GPIO, 2 extra analog inputs, 28K of flash, and 2K of RAM. It has onboard USB bootloading support with Optiboot support, so you can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
