# Fritzing sketch phoneCodeOscillatorTrinketPro (saved by Fritzing 0.9.2b)
circuit board: 3.37521cm x 3.10714cm
breadboards: 1

parts:
  J1 = Piezo Speaker
  C1 = Ceramic Capacitor [capacitance=10µF package="100 mil [THT, multilayer]"]
  R1 = Trimmer Potentiometer [maximum_resistance=10kΩ package=THT]
  C2 = Ceramic Capacitor [capacitance=0.1µF package="100 mil [THT, multilayer]"]
  R2 = Resistor [tolerance=±5% resistance=68 package=THT]
  TRS1 = Audio Jack (TRS) 3.5mm [package="4Ucon 08780 [THT]"]
  JP1 = Header 2 [package=jst-2-pth-ns]
  S1 = Toggle Switch [package=THT]
  J2 = female pin header, 2 pins [form="♀ (female)"]
  J3 = female pin header, 2 pins [form="♀ (female)"]
  J4 = female pin header, 2 pins [form="♀ (female)"]
  Part1 = Arduino Uno (Rev3)
  Part2 = TRRS 3.5mm Jack Breakout

nets:
  N1: J1.pin1, R1.leg2, C2.1, TRS1.Sleeve, JP1.1, JP1.2, S1.L2, J2.pin1, Part1.GND, Part2.SLEEVE
  N2: J1.pin2, C1.1, Part2.TIP
  N3: C1.0, R1.wiper
  N4: R1.leg1, C2.0, R2.Pin_1
  N5: R2.Pin_0, J3.pin2
  N6: TRS1.Ring, J4.pin1, Part1.D3_PWM
  N7: TRS1.Tip, J4.pin2, Part1.D2
  N8: S1.COM, J2.pin2, Part1.VIN
